// Logisim project Experiment 2.circ as structural Verilog: 1 circuit, main circuit main
module main (
  input  I2,
  input  I4,
  input  I6,
  input  I7,
  input  I10,
  input  I11,
  input  I12,
  input  I13,
  input  [3:0] in_9,
  output out_10
);

  Multiplexer #(.select(4)) multiplexer_1 (
    .in0(1'b1), .in1(1'b1), .in2(I2), .in3(1'b1), .in4(I4), .in5(1'b1), .in6(I6), .in7(I7), .in8(1'b1),
    .in9(1'b1), .in10(I10), .in11(I11), .in12(I12), .in13(I13), .in14(1'b1), .in15(1'b1), .out(out_10),
    .sel(in_9));  // open: en

  // Notes on the sheet:
  //   I0
  //   I1
  //   I3
  //   I5
  //   I8
  //   I9
  //   I14
  //   I15
endmodule
